# Fritzing sketch ESP8266-e-LM35 (saved by Fritzing 0.9.10b)
breadboards: 1

parts:
  T1 = LM35 Temperature Sensor [package="TO92 [THT]"]
  Mod1 = Amica NodeMCU DEVKIT 1.0

nets:
  N1: T1.+Vs, Mod1.pin1, Mod1.pin_10, Mod1.pin_26
  N2: T1.Vout, Mod1.pin_16
  N3: T1.GND, Mod1.pin2, Mod1.pin_9, Mod1.pin_25, Mod1.pin_29

// code stored in the sketch: Untitled.bas

void setup() 


{


Serial.begin(115200); 


}





void loop() 


{


int valorObtido = analogRead(A0);


float milivolts = (valorObtido/1024.0) * 3300; 


float celsius = milivolts/10;


Serial.print("A temperatura é de = ");


Serial.println(celsius);




}
